# Fritzing sketch PiezoRGBledProMini9V (saved by Fritzing 0.9.2b)
circuit board: 3.03975cm x 3.66426cm
breadboards: 1

parts:
  Part2 = Arduino Pro Mini v13
  Piezo_element = Piezo Speaker
  R1 = Resistor [tolerance=±5% resistance=1M package=THT]
  VCC1 = Battery block 9V
  RGB_led1 = RGB LED - (4 legs) [package="5 mm [THT]"]
  part = Resistor [tolerance=±5% resistance=330 package=THT]
  part_2 = Resistor [tolerance=±5% resistance=330 package=THT]
  part_3 = Resistor [tolerance=±5% resistance=330 package=THT]

nets:
  N1: Part2.VCC, RGB_led1.common_anode
  N2: Part2.RAW, VCC1.+
  N3: Part2.GND, Piezo_element.pin1, R1.Pin_1, VCC1.-
  N4: Part2.A0, Piezo_element.pin2, R1.Pin_0
  N5: Part2.D6_PWM, part_3.Pin_1
  N6: Part2.D5_PWM, part_2.Pin_1
  N7: Part2.D3_PWM, part.Pin_1
  N8: RGB_led1.red_cathode, part_3.Pin_0
  N9: RGB_led1.green_cathode, part_2.Pin_0
  N10: RGB_led1.blue_cathode, part.Pin_0
